# Fritzing sketch rasp-ada (saved by Fritzing 0.9.3b)
breadboards: 1

parts:
  Raspberry_Pi1 = Raspberry Pi 2
  R3 = Resistor [tolerance=±5% resistance=330 package=THT]
  R4 = Resistor [tolerance=±5% resistance=330 package=THT]
  LED3 = LED - 5mm [color="Red (633nm)" package="5 mm [THT]"]
  LED4 = LED - 5mm [color="Green (565nm)" package="5 mm [THT]"]

nets:
  N1: Raspberry_Pi1.GPIO17, LED4.cathode
  N2: Raspberry_Pi1.GPIO27, LED3.cathode
  N3: Raspberry_Pi1.GND, R3.Pin_0, R4.Pin_0
  N4: R3.Pin_1, LED3.anode
  N5: R4.Pin_1, LED4.anode
